# Fritzing sketch layout (saved by Fritzing 0.9.3b)
breadboards: 1

parts:
  Raspberry_Pi_1 = Raspberry Pi 3 [part_number=RPI-3-V1.2]
  LED1 = LED - 5mm [color="Green (560nm)" package="5 mm [THT]"]
  R1 = Resistor [tolerance=±5% resistance=330 package=THT]
  S2 = Pushbutton [package="[THT]"]

nets:
  N1: Raspberry_Pi_1.GPIO3, S2.Pin_3, S2.Pin_4
  N2: Raspberry_Pi_1.GIPO4, R1.Pin_1
  N3: Raspberry_Pi_1.GND, LED1.cathode, S2.Pin_1, S2.Pin_2
  N4: LED1.anode, R1.Pin_0
